# Fritzing sketch EMDR V2 (saved by Fritzing 0.9.3b)
circuit board: 9.2cm x 6.5cm
breadboards: 1

parts:
  LLC1 = Logic Level Converter [package="Breakout board"]
  R0 = Rotary Potentiometer (Large) [maximum_resistance=100kΩ package=THT]
  F2 = Resettable Fuse PTC [part_number=500mA package=ptc]
  J1 = Power Jack [package=power_jack_slot]
  J2 = screw terminal, 3 pins
  J4 = screw terminal, 2 pins
  C1 = Electrolytic Capacitor [capacitance=1mF voltage=63V package="300 mil [THT, electrolytic]"]
  WeMos_D1_Mini2 = WeMos D1 Mini
  R1 = Resistor [tolerance=±5% resistance=330 package=THT]
  WeMos_D1_Mini1 = WeMos D1 Mini
  J3 = female pin header, 4 pins [form="♀ (female)"]
  R2 = Resistor [tolerance=±5% resistance=4.7k package=THT]
  R3 = Resistor [tolerance=±5% resistance=4.7k package=THT]
  R4 = Resistor [tolerance=±5% resistance=10k package=THT]
  R5 = Resistor [tolerance=±5% resistance=10k package=THT]
  5v = Pad [width=5 height=5 connect=center]
  Gnd = Pad [width=5 height=5 connect=center]
  Pad3 = Pad [width=3 height=3 connect=center]
  F1 = Resettable Fuse PTC [part_number=5A package=ptc]
  R6 = Resistor [tolerance=±5% resistance=10k package=THT]
  R7 = Resistor [tolerance=±5% resistance=10k package=THT]
  SW1 = DIP SWITCH [package=dipswitch-02]
  SW2 = DIP SWITCH [package=dipswitch-02]
  S2 = Momentary Switch [package=ksa_sealed_tac_switch]

nets:
  N1: LLC1.LV1, WeMos_D1_Mini1.D4
  N2: LLC1.LV, R0.leg1, WeMos_D1_Mini1.3V3, J3.pin2, R2.Pin_0, R3.Pin_0, R4.Pin_0, R5.Pin_0, Pad3.pad, R6.Pin_0, R7.Pin_0
  N3: LLC1.L-GND, LLC1.H-GND, R0.leg2, J1.GNDBREAK, J1.GND, J2.pin3, C1.-, WeMos_D1_Mini1.G, J3.pin1, Gnd.pad, SW1.1, SW1.2, SW2.1, SW2.2, S2.3
  5V: LLC1.HV, F2.1, WeMos_D1_Mini2.5V, WeMos_D1_Mini1.5V
  N4: LLC1.HV1, R1.Pin_0
  N5: R0.wiper, WeMos_D1_Mini1.A0
  N6: F2.2, J1.PWR, F1.2
  N7: J2.pin1, J4.pin1, 5v.pad
  N8: J2.pin2, R1.Pin_1
  N9: J4.pin2, C1.+, F1.1
  N10: WeMos_D1_Mini2.D1, WeMos_D1_Mini1.D8
  N11: WeMos_D1_Mini1.D0, R7.Pin_1, SW2.4
  N12: WeMos_D1_Mini1.D1, J3.pin3, R3.Pin_1
  N13: WeMos_D1_Mini1.D2, J3.pin4, R2.Pin_1
  N14: WeMos_D1_Mini1.D3, S2.1
  N15: WeMos_D1_Mini1.D5, R6.Pin_1, SW2.3
  N16: WeMos_D1_Mini1.D6, R4.Pin_1, SW1.4
  N17: WeMos_D1_Mini1.D7, R5.Pin_1, SW1.3

notes:
  Gnd
  5v
  3v
  Speed
  SDA
  COM
  SCL
  NO
  Rx
  Tx
  reset
  D1

custom parts:
  Logic Level Converter: 5V to/from 3.3V logic level converter
